// Logisim project MA_Stage.circ as structural Verilog: 1 circuit, main circuit MA
module MA (
  input  [31:0] data,
  input  [31:0] OP2,
  input  RW__MA_op2,
  input  [31:0] aluResult,
  input  Reset,
  input  isSt,
  input  isLd,
  input  Clock,
  output [31:0] ldResult
);

  wire [31:0] multiplexer_1_out, ram_1_data;

  Multiplexer #(.width(32)) multiplexer_1 (
    .in0(data), .in1(OP2), .out(multiplexer_1_out), .sel(RW__MA_op2));  // open: en
  RAM #(.addrWidth(24), .dataWidth(32), .bus("separate")) ram_1 (
    .addr(aluResult[25:2]), .din(multiplexer_1_out), .data(ram_1_data), .str(isSt), .clk(Clock), .ld(isLd),
    .clr(Reset));  // open: sel

  // Notes on the sheet:
  //   Reset: pull=down
  //   Clock: pull=down
  //   aluResult: pull=down
  //   RW__MA_op2: pull=down
  //   data: pull=down
  //   isSt: pull=down
  //   isLd: pull=down
  //   OP2: pull=down
endmodule
