// Logisim project IF_Stage.circ as structural Verilog: 1 circuit, main circuit IF
// IF Stage
module IF (
  input  isBranchTaken,
  input  [31:0] BranchPC,
  input  Stall,
  input  Clock,
  input  Reset,
  output [31:0] Instruction,
  output [31:0] PC
);

  wire [31:0] adder_1_out, multiplexer_1_out;

  Register #(.width(32)) u_PC (.D(multiplexer_1_out), .en(Stall), .Q(PC), .clk(Clock), .clr(Reset));
  Multiplexer #(.width(32), .enable("false")) multiplexer_1 (
    .in0(adder_1_out), .in1(BranchPC), .out(multiplexer_1_out), .sel(isBranchTaken));
  Adder #(.width(32)) adder_1 (.a(32'h4), .b(PC), .out(adder_1_out));  // open: cin, cout
  ROM #(.addrWidth(24), .dataWidth(32)) rom_1 (.addr(PC[25:2]), .data(Instruction));  // open: sel

  // Notes on the sheet:
  //   isBranchTaken: pull=down
  //   Stall: pull=down
  //   Clock: pull=down
  //   Reset: pull=down
  //   Instruction Memory
endmodule
